# Fritzing sketch PING_SENSOR (saved by Fritzing 0.9.3b)
breadboards: 1

parts:
  Grove1 = Grove OLED 128x96
  Part1 = Arduino Uno (Rev3)
  Part2 = SRF05 Ultrasonic Rangefinder

nets:
  GND: Grove1.GND, Part1.GND, Part2.GND
  VCC: Grove1.VCC, Part1.5V, Part2.VCC
  N1: Grove1.SDA, Part1.A4/SDA
  N2: Grove1.SCL, Part1.A5/SCL
  N3: Part1.D11_PWM/MOSI, Part2.Trig
